# Fritzing sketch Untitled Sketch (saved by Fritzing 0.8.7b)
breadboards: 1

parts:
  元件1 = Arduino Uno (Rev3)
  R1 = Resistor [tolerance=±5% resistance=10k package=THT]
  S1 = Pushbutton [package="[THT]"]
  LED1 = RGB LED (com. anode, rbg) [package="5 mm [THT]"]
  R2 = Resistor [tolerance=±5% resistance=220 package=THT]
  R3 = Resistor [tolerance=±5% resistance=220 package=THT]
  R4 = Resistor [tolerance=±5% resistance=220 package=THT]
  J1 = Piezo Speaker
  R5 = Resistor [tolerance=±5% resistance=220 package=THT]

nets:
  N1: 元件1.D10_PWM/SS, J1.pin2
  N2: 元件1.D11_PWM/MOSI, R4.Pin_0
  N3: 元件1.D12/MISO, R3.Pin_0
  N4: 元件1.D13/SCK, R2.Pin_0
  N5: 元件1.D2, R1.Pin_1, S1.Pin_3, S1.Pin_4
  N6: 元件1.5V, S1.Pin_1, S1.Pin_2
  N7: 元件1.GND, R1.Pin_0, LED1.blue_cathode, R5.Pin_0
  N8: LED1.red_cathode, R4.Pin_1
  N9: LED1.common_anode, R3.Pin_1
  N10: LED1.green_cathode, R2.Pin_1
  N11: J1.pin1, R5.Pin_1
